# Fritzing sketch p1_blink (saved by Fritzing 0.9.3b)
breadboards: 1

parts:
  Part2 = Arduino Mega 2560 (Rev3)
  S1 = Pushbutton [package="[SMD]"]
  S2 = Pushbutton [package="[SMD]"]
  S3 = Pushbutton [package="[SMD]"]
  S4 = Pushbutton [package="[SMD]"]
  R1 = Resistor [tolerance=±5% resistance=220 package="0805 [SMD]"]
  R2 = Resistor [tolerance=±5% resistance=220 package="0805 [SMD]"]
  R3 = Resistor [tolerance=±5% resistance=220 package="0805 [SMD]"]
  R4 = Resistor [tolerance=±5% resistance=220 package="0805 [SMD]"]
  R5 = Resistor [tolerance=±5% resistance=220 package="0805 [SMD]"]
  R6 = Resistor [tolerance=±5% resistance=220 package="0805 [SMD]"]
  R7 = Resistor [tolerance=±5% resistance=220 package="0805 [SMD]"]
  R8 = Resistor [tolerance=±5% resistance=220 package="0805 [SMD]"]
  R15 = Resistor [tolerance=±5% resistance=10k package="0805 [SMD]"]
  R16 = Resistor [tolerance=±5% resistance=10k package="0805 [SMD]"]
  R17 = Resistor [tolerance=±5% resistance=10k package="0805 [SMD]"]
  R18 = Resistor [tolerance=±5% resistance=10k package="0805 [SMD]"]
  LED17 = smd LED [color="Green (560nm)" package="0603 [SMD]"]
  LED18 = smd LED [color="Green (560nm)" package="0603 [SMD]"]
  LED19 = smd LED [color="Green (560nm)" package="0603 [SMD]"]
  LED20 = smd LED [color="Green (560nm)" package="0603 [SMD]"]
  LED21 = smd LED [color="Yellow (585nm)" package="0603 [SMD]"]
  LED22 = smd LED [color="Yellow (585nm)" package="0603 [SMD]"]
  LED23 = smd LED [color="Yellow (585nm)" package="0603 [SMD]"]
  LED24 = smd LED [color="Yellow (585nm)" package="0603 [SMD]"]
  LED25 = smd LED [color="Blue (470nm)" package="0603 [SMD]"]
  LED26 = smd LED [color="Blue (470nm)" package="0603 [SMD]"]
  LED27 = smd LED [color="Blue (470nm)" package="0603 [SMD]"]
  LED28 = smd LED [color="Blue (470nm)" package="0603 [SMD]"]
  LED29 = smd LED [color="Red (635nm)" package="0603 [SMD]"]
  LED30 = smd LED [color="Red (635nm)" package="0603 [SMD]"]
  LED31 = smd LED [color="Red (635nm)" package="0603 [SMD]"]
  LED32 = smd LED [color="Red (635nm)" package="0603 [SMD]"]

nets:
  N1: Part2.5V, S1.Pin_3, S1.Pin_4, S2.Pin_3, S2.Pin_4, S3.Pin_3, S3.Pin_4, S4.Pin_3, S4.Pin_4
  N2: Part2.GND, R1.Pin_0, R2.Pin_0, R3.Pin_0, R4.Pin_0, R5.Pin_0, R6.Pin_0, R7.Pin_0, R8.Pin_0, R15.Pin_1, R16.Pin_1, R17.Pin_1, R18.Pin_1
  N3: Part2.D46, S4.Pin_1, S4.Pin_2, R18.Pin_0
  N4: Part2.D47, S3.Pin_1, S3.Pin_2, R17.Pin_0
  N5: Part2.D48, S2.Pin_1, S2.Pin_2, R15.Pin_0
  N6: Part2.D49, S1.Pin_1, S1.Pin_2, R16.Pin_0
  N7: Part2.D50, LED17.anode, LED18.anode, LED19.anode, LED20.anode
  N8: Part2.D51, LED21.anode, LED22.anode, LED23.anode, LED24.anode
  N9: Part2.D52, LED25.anode, LED26.anode, LED27.anode, LED28.anode
  N10: Part2.D53, LED29.anode, LED30.anode, LED31.anode, LED32.anode
  N11: R1.Pin_1, LED30.cathode, LED32.cathode
  N12: R2.Pin_1, LED29.cathode, LED31.cathode
  N13: R3.Pin_1, LED26.cathode, LED28.cathode
  N14: R4.Pin_1, LED25.cathode, LED27.cathode
  N15: R5.Pin_1, LED22.cathode, LED24.cathode
  N16: R6.Pin_1, LED21.cathode, LED23.cathode
  N17: R7.Pin_1, LED18.cathode, LED20.cathode
  N18: R8.Pin_1, LED17.cathode, LED19.cathode
