# Fritzing sketch the_human_touch (saved by Fritzing 0.9.3b)
breadboards: 1

parts:
  Part1 = Arduino Mega 2560 (Rev3)
  HC-SR04_Sensor_1 = HC-SR04 Ultrasonic Distance Sensor

nets:
  5V: Part1.5V, HC-SR04_Sensor_1.VCC
  GND: Part1.GND, HC-SR04_Sensor_1.GND
  N1: Part1.D52, HC-SR04_Sensor_1.TRIG
  N2: Part1.D53, HC-SR04_Sensor_1.ECHO
